# Fritzing sketch cam-trigger (saved by Fritzing 0.9.3b)
circuit board: 8.46667cm x 5.64444cm
breadboards: 1

parts:
  LCD1 = LCD screen
  Part1 = Arduino Uno (Rev3)
  R1 = Rotary Potentiometer (Small) [maximum_resistance=10kΩ package=THT]
  R2 = Rotary Potentiometer (Small) [maximum_resistance=10kΩ package=THT]
  R3 = Resistor [tolerance=±5% resistance=220 package=THT]

nets:
  VSS: LCD1.VSS, LCD1.R/W, LCD1.LED-, Part1.GND, R1.leg1, R2.leg1
  VDD: LCD1.VDD, Part1.5V, R1.leg2, R2.leg2, R3.Pin_1
  N1: LCD1.V0, R2.wiper
  N2: LCD1.RS, Part1.D7
  N3: LCD1.E, Part1.D8
  N4: LCD1.DB4, Part1.D9_PWM
  N5: LCD1.DB5, Part1.D10_PWM/SS
  N6: LCD1.DB6, Part1.D11_PWM/MOSI
  N7: LCD1.DB7, Part1.D12/MISO
  N8: LCD1.LED+, R3.Pin_0
  N9: Part1.A2, R1.wiper

notes:
  camera

// code stored in the sketch: cam-trigger.ino
#include <Arduino.h>
#include <LiquidCrystal.h>


int pwm_pin = 6;
LiquidCrystal lcd(7, 8, 9, 10, 11, 12);
int pot_time = 2;
float time = 2.0;
float trigger_time_ms = 200;


void setup() {
  lcd.begin(16, 2);
 	lcd.print("Starting");
  delay(2000);
}


void loop() {
  lcd.clear();
  lcd.setCursor(0, 0);
  time = analogRead(pot_time) / 200.0 + 1.5;
  lcd.print("time: ");
  lcd.print(time);


  analogWrite(pwm_pin, 255);
  delay(time * 1000);
  // trigger
  analogWrite(pwm_pin, 0);
  delay(trigger_time_ms);
}
